# Fritzing sketch snakeCircuit (saved by Fritzing 0.9.3b)

parts:
  Part1 = Matrix LED de 8x8 basada en MAX7219
  Part2 = Arduino Uno (Rev3)

nets:
  GND: Part1.GND, Part2.GND
  N1: Part1.CS, Part2.D10_PWM/SS
  N2: Part1.CLK, Part2.D11_PWM/MOSI
  N3: Part1.DIN, Part2.D12/MISO
